# Fritzing sketch pump_ctrl (saved by Fritzing 0.8.5b)
breadboards: 1

parts:
  Composants1 = Arduino Uno (Rev3)
  M1 = DC Motor
  K1 = Relay [part_number=FRS1B-S package=THT]  # not connected
  K2 = Relay [part_number=FRS1B-S package=THT]
  S1 = Reed switch [package=THT]
  R1 = Resistor [tolerance=±5% resistance=10k package=THT]
  C1 = Ceramic Capacitor [capacitance=22nF package="100 mil [THT, multilayer]"]
  R2 = Resistor [tolerance=±5% resistance=1M package=THT]
  U1 = CNZ1120 [package=cnz1120]
  R3 = Resistor [tolerance=±5% resistance=470 package=THT]
  R4 = Resistor [tolerance=±5% resistance=470 package=THT]

nets:
  N1: Composants1.A0, R2.Pin_0
  N2: Composants1.GND, K2.A, K2.COIL1, R1.Pin_1, C1.1, R2.Pin_1, U1.4, R4.Pin_0
  N3: Composants1.D2, U1.3, R4.Pin_1
  N4: Composants1.D3_PWM, Composants1.5V, K2.B, S1.pin_2, U1.2, R3.Pin_0
  N5: Composants1.D5_PWM, K2.COIL2
  N6: M1.pin_1, K2.C1, K2.C2
  N7: S1.pin_1, R1.Pin_0, C1.0
  N8: U1.1, R3.Pin_1

notes:
  moteur de la pompe péristaltique
  ILS du moteur
  (compte-tours)
  capteur de niveau d'eau
  (mi-marée)
  capteur optique du moteur
  (compte-tours)
